// Logisim project FunSel Register.circ as structural Verilog
module _8bit_FunSel_Register (
  input  in_1,
  input  Sel,
  input  Fun,
  input  [7:0] I_MSB,
  output [7:0] Q_MSB
);

  wire adder_1_cout, and_1_out, and_2_out, and_3_out, and_4_out, and_5_out, and_6_out, and_7_out, and_8_out,
       and_9_out, and_10_out, clock_1_out, decoder_1_out1, decoder_1_out2, decoder_1_out3, multiplexer_1_out,
       multiplexer_2_out, multiplexer_3_out, multiplexer_4_out, multiplexer_5_out, multiplexer_6_out,
       multiplexer_7_out, multiplexer_8_out, or_1_out;
  wire [1:1] not_1_out;
  wire [7:0] adder_1_out, xor_1_out;

  xor xor_1 (xor_1_out[0], 1'b1, decoder_1_out1);
  xor xor_2 (xor_1_out[7], 1'b0, decoder_1_out1);
  Decoder #(.select(2), .enable("false")) decoder_1 (
    .out1(decoder_1_out1), .out2(decoder_1_out2), .out3(decoder_1_out3), .sel({Fun, Sel}));  // open: out0
  Adder adder_1 (
    .a(Q_MSB), .b({{7{xor_1_out[7]}}, xor_1_out[0]}), .out(adder_1_out), .cin(decoder_1_out1),
    .cout(adder_1_cout));
  or or_1 (or_1_out, decoder_1_out1, decoder_1_out2);
  and and_1 (and_1_out, or_1_out, in_1);
  and and_2 (and_2_out, adder_1_out[0], and_1_out);
  and and_3 (and_3_out, adder_1_out[1], and_1_out);
  and and_4 (and_4_out, adder_1_out[2], and_1_out);
  and and_5 (and_5_out, adder_1_out[3], and_1_out);
  and and_6 (and_6_out, adder_1_out[4], and_1_out);
  and and_7 (and_7_out, adder_1_out[5], and_1_out);
  and and_8 (and_8_out, adder_1_out[6], and_1_out);
  and and_9 (and_9_out, adder_1_out[7], and_1_out);
  Multiplexer #(.select(2), .enable("false")) multiplexer_1 (
    .in0(Q_MSB[0]), .in1(and_2_out), .in2(Q_MSB[0]), .in3(I_MSB[0]), .out(multiplexer_1_out),
    .sel({not_1_out[1], in_1}));
  Multiplexer #(.select(2), .enable("false")) multiplexer_2 (
    .in0(Q_MSB[1]), .in1(and_3_out), .in2(Q_MSB[1]), .in3(I_MSB[1]), .out(multiplexer_2_out),
    .sel({not_1_out[1], in_1}));
  Multiplexer #(.select(2), .enable("false")) multiplexer_3 (
    .in0(Q_MSB[2]), .in1(and_4_out), .in2(Q_MSB[2]), .in3(I_MSB[2]), .out(multiplexer_3_out),
    .sel({not_1_out[1], in_1}));
  Multiplexer #(.select(2), .enable("false")) multiplexer_4 (
    .in0(Q_MSB[3]), .in1(and_5_out), .in2(Q_MSB[3]), .in3(I_MSB[3]), .out(multiplexer_4_out),
    .sel({not_1_out[1], in_1}));
  Multiplexer #(.select(2), .enable("false")) multiplexer_5 (
    .in0(Q_MSB[4]), .in1(and_6_out), .in2(Q_MSB[4]), .in3(I_MSB[4]), .out(multiplexer_5_out),
    .sel({not_1_out[1], in_1}));
  Multiplexer #(.select(2), .enable("false")) multiplexer_6 (
    .in0(Q_MSB[5]), .in1(and_7_out), .in2(Q_MSB[5]), .in3(I_MSB[5]), .out(multiplexer_6_out),
    .sel({not_1_out[1], in_1}));
  Multiplexer #(.select(2), .enable("false")) multiplexer_7 (
    .in0(Q_MSB[6]), .in1(and_8_out), .in2(Q_MSB[6]), .in3(I_MSB[6]), .out(multiplexer_7_out),
    .sel({not_1_out[1], in_1}));
  Multiplexer #(.select(2), .enable("false")) multiplexer_8 (
    .in0(Q_MSB[7]), .in1(and_9_out), .in2(Q_MSB[7]), .in3(I_MSB[7]), .out(multiplexer_8_out),
    .sel({not_1_out[1], in_1}));
  not not_1 (not_1_out[1], or_1_out);
  and and_10 (and_10_out, in_1, decoder_1_out3);
  Clock clock_1 (.out(clock_1_out));
  D_Flip_Flop d_ff_1 (
    .clk(clock_1_out), .D(multiplexer_1_out), .Q(Q_MSB[0]), .preset(1'b0), .reset(and_10_out));  // open: Qn
  D_Flip_Flop d_ff_2 (
    .clk(clock_1_out), .D(multiplexer_2_out), .Q(Q_MSB[1]), .preset(1'b0), .reset(and_10_out));  // open: Qn
  D_Flip_Flop d_ff_3 (
    .clk(clock_1_out), .D(multiplexer_3_out), .Q(Q_MSB[2]), .preset(1'b0), .reset(and_10_out));  // open: Qn
  D_Flip_Flop d_ff_4 (
    .clk(clock_1_out), .D(multiplexer_4_out), .Q(Q_MSB[3]), .preset(1'b0), .reset(and_10_out));  // open: Qn
  D_Flip_Flop d_ff_5 (
    .clk(clock_1_out), .D(multiplexer_5_out), .Q(Q_MSB[4]), .preset(1'b0), .reset(and_10_out));  // open: Qn
  D_Flip_Flop d_ff_6 (
    .clk(clock_1_out), .D(multiplexer_6_out), .Q(Q_MSB[5]), .preset(1'b0), .reset(and_10_out));  // open: Qn
  D_Flip_Flop d_ff_7 (
    .clk(clock_1_out), .D(multiplexer_7_out), .Q(Q_MSB[6]), .preset(1'b0), .reset(and_10_out));  // open: Qn
  D_Flip_Flop d_ff_8 (
    .clk(clock_1_out), .D(multiplexer_8_out), .Q(Q_MSB[7]), .preset(1'b0), .reset(and_10_out));  // open: Qn

  // Notes on the sheet:
  //   I
  //   I:LSB
  //   Enable
  //   CLK
  //   LSB
  //   MSB
  //   Reset
  //   Cout
  //   Q:LSB
  //   Q
endmodule
