// Logisim project au.circ as structural Verilog: 1 circuit, main circuit main
module main (
  input  [7:0] A,
  input  [7:0] B,
  input  Carry_In,
  input  [1:0] FunSel,
  output [7:0] Output,
  output Carry_Out,
  output Overflow
);


  assign Carry_Out = Carry_In;
endmodule
