// Logisim project project2.circ as structural Verilog: 1 circuit, main circuit ALU
module ALU (
  input  [7:0] A,
  input  [7:0] B,
  input  [3:0] FunSel
);

  wire [7:0] and_1_out, not_1_out, not_2_out, or_1_out, xor_1_out;

  assign and_1_out = A & B;  // AND_Gate and_1, 8 bits wide
  assign or_1_out = A | B;  // OR_Gate or_1, 8 bits wide
  assign not_1_out = ~A;  // NOT_Gate not_1, 8 bits wide
  assign xor_1_out = A ^ B;  // XOR_Gate xor_1, 8 bits wide
  assign not_2_out = ~B;  // NOT_Gate not_2, 8 bits wide
  Multiplexer #(.select(4), .width(8), .enable("false")) multiplexer_1 (.sel(FunSel));  // open: in0, in1, in2, in3, in4, in5, in6, in7, in8, in9, in10, in11, in12, in13, in14, in15, out

  // Notes on the sheet:
  //   A AND B
  //   A OR B
  //   NOT A
  //   A XOR B
  //   B
  //   NOT B
endmodule
